# Fritzing sketch GSM (saved by Fritzing 0.9.3b)
breadboards: 1

parts:
  GSM_Module = SIM800L [package=THT]
  Part1 = Arduino Mega 2560 (Rev3)

nets:
  N1: GSM_Module.5V, Part1.IOREF
  N2: GSM_Module.SIM_TXD, Part1.D15/RX3
  N3: GSM_Module.SIM_RXD, Part1.D14/TX3
  GND: GSM_Module.GND, Part1.GND
  N4: GSM_Module.RST, Part1.D5_PWM
