# Fritzing sketch fishfeeder + button (saved by Fritzing 0.9.3b)
breadboards: 1

parts:
  Part1 = Arduino Mega 2560 (Rev3)
  J1 = Basic Servo
  V1 = DC Power [voltage=12V]
  S1 = SWITCH-MOMENTARY-2 [package=tactile-pth]
  LED1 = LED - 5mm [color="Red (633nm)" package="5 mm [THT]"]
  R1 = Resistor [tolerance=±5% resistance=220 package=THT]

nets:
  GND: Part1.GND, J1.gnd, V1.V-, S1.2, R1.Pin_1
  N1: Part1.D9_PWM, S1.1
  N2: Part1.D8_PWM, J1.pulse
  N3: Part1.D26, LED1.anode
  N4: J1.vcc, V1.V+
  N5: LED1.cathode, R1.Pin_0
