# Fritzing sketch relay+button+pump (saved by Fritzing 0.9.3b)
breadboards: 1

parts:
  Part2 = Arduino Mega 2560 (Rev3)
  U1 = RELAY-SOLIDSTATE [package=relay-s108t02]
  U2 = RELAY-SOLIDSTATE [package=relay-s108t02]
  V1 = AC Power [voltage=5 frequency=60]
  M1 = DC Motor
  M2 = DC Motor
  S1 = SWITCH-MOMENTARY-2 [package=tactile-pth]
  LED1 = smd LED [color="Red (633nm)" package="1206 [SMD]"]
  R1 = Resistor [tolerance=±5% resistance=1k package=THT]

nets:
  N1: Part2.D11_PWM, S1.1
  N2: Part2.5V, U1.-, U2.-
  N3: Part2.GND, S1.2, R1.Pin_1
  N4: Part2.D28, LED1.anode
  N5: Part2.D46, U1.+
  N6: Part2.D48, U2.+
  N7: U1.T1, M1.pin_1
  N8: U1.T2, U2.T2, V1.V-
  N9: U2.T1, M2.pin_1
  N10: V1.V+, M1.pin_2, M2.pin_2
  N11: LED1.cathode, R1.Pin_0
