# Fritzing sketch sensor + lcd + buttons (saved by Fritzing 0.9.3b)
breadboards: 1

parts:
  U1 = TMP36 [package=to-92]
  U2 = TMP36 [package=to-92]
  S1 = SWITCH-MOMENTARY-2 [package=tactile-pth]
  U3 = LCD-16X2 [package=lcd-8x2]
  R1 = Trimmer Potentiometer [maximum_resistance=10kΩ package=THT]
  Part1 = Arduino Mega 2560 (Rev3)

nets:
  VCC: U1.VCC, U3.VDD, U3.A, R1.leg2, Part1.IOREF
  N1: U1.VOUT, Part1.D4_PWM
  GND: U1.GND, U2.GND, S1.2, U3.VSS, U3.R_W, U3.K, R1.leg1, Part1.GND
  VCC_2: U2.VCC, Part1.5V
  N2: U2.VOUT, Part1.A8
  N3: S1.1, Part1.D13_PWM
  N4: U3.VO, R1.wiper
  N5: U3.RS, Part1.A4
  N6: U3.E, Part1.A5
  N7: U3.DB4, Part1.A3
  N8: U3.DB5, Part1.A2
  N9: U3.DB6, Part1.A1
  N10: U3.DB7, Part1.A0
